# Fritzing sketch WindowControll (saved by Fritzing 0.7.7b)
breadboards: 1

parts:
  Arduino1 = Arduino
  LCD1 = LCD screen
  IR_Reciever_(TSOP22)1 = IR Reciever
  PIR1 = PIR sensor
  DHT1 = DHT11 Humitidy and Temperature Sensor
  LED1 = LED - 5mm [color="Red (660nm)" package="5 mm [THT]"]
  LED2 = LED - 5mm [color="Green (565nm)" package="5 mm [THT]"]
  LED3 = LED - 5mm [color="Blue (430nm)" package="5 mm [THT]"]
  R1 = Resistor [tolerance=±5% resistance=220 package=THT]
  R2 = Resistor [tolerance=±5% resistance=220 package=THT]
  R3 = Resistor [tolerance=±5% resistance=220 package=THT]
  J1 = Basic Servo
  J2 = Basic Servo

nets:
  GND: Arduino1.GND, LCD1.VSS, LCD1.DB5, LCD1.DB7, LCD1.LED-, IR_Reciever_(TSOP22)1.GND, PIR1.GND, DHT1.GND, R1.Pin_1, R2.Pin_1, R3.Pin_1, J1.gnd, J2.gnd
  N1: Arduino1.D12, LCD1.DB6
  N2: Arduino1.D11, LED3.anode
  N3: Arduino1.D10, LED1.anode
  N4: Arduino1.D9, LED2.anode
  N5: Arduino1.D8, LCD1.DB4
  N6: Arduino1.D7, LCD1.E
  N7: Arduino1.D6, LCD1.R/W
  N8: Arduino1.D5, LCD1.RS
  N9: Arduino1.D4, LCD1.V0
  N10: Arduino1.D3, PIR1.SIG
  N11: Arduino1.D2, IR_Reciever_(TSOP22)1.OUT
  VDD: Arduino1.+5V, LCD1.VDD, LCD1.LED+, IR_Reciever_(TSOP22)1.Vs, PIR1.VDD, DHT1.VDD
  VCC: Arduino1.VIN, J1.vcc, J2.vcc
  N12: Arduino1.A0, DHT1.DATA
  N13: Arduino1.A1, J2.pulse
  N14: Arduino1.A2, J1.pulse
  N15: LED1.cathode, R2.Pin_0
  N16: LED2.cathode, R3.Pin_0
  N17: LED3.cathode, R1.Pin_0

notes:
  PIR подключен к PD3 через Troika Shield
  DHT подключен к A0 через Troika Shield

custom parts:
  IR Reciever: Basic infrared reciever
  DHT11 Humitidy and Temperature Sensor: DHT11 Humidity and Temperature Sensor
